# Fritzing sketch Diseño Proto y esquematico Práctica 1 (saved by Fritzing 0.9.3b)
breadboards: 1

parts:
  Potenciómetro_10K = POT [package=pot_mammoth]
  part = Arduino Nano (Rev3.0)

nets:
  N1: Potenciómetro_10K.S, part.3V3
  N2: Potenciómetro_10K.A, part.A0
  N3: Potenciómetro_10K.E, part.GND
